# Fritzing sketch esp_pract (saved by Fritzing 0.9.4)
breadboards: 1

parts:
  U1 = NodeMCU V1.0  # not connected
  R4 = Resistor [tolerance=±5% resistance=220 package=THT]  # not connected
  7_Segment1 = 7 Segment Display  # not connected
  R2 = Resistor [tolerance=±5% resistance=1k package=THT]  # not connected
  S1 = Pushbutton [package="[THT]"]
  LED1 = LED - 5mm [color="Red (633nm)" package="5 mm [THT]"]  # not connected
  LED2 = LED - 5mm [color="Green (560nm)" package="5 mm [THT]"]  # not connected
  LED3 = LED - 5mm [color="Yellow (595nm)" package="5 mm [THT]"]  # not connected
  R5 = Resistor [tolerance=±5% resistance=220 package=THT]  # not connected
  R6 = Resistor [tolerance=±5% resistance=220 package=THT]  # not connected
  J1 = DHT11 basic temperature-humidity sensor [form="♂ (male)" package=THT]  # not connected

nets:
  N1: S1.Pin_1, S1.Pin_2
  N2: S1.Pin_3, S1.Pin_4

custom parts:
  NodeMCU V1.0: ESP8266 based NodeMCU
  DHT11 basic temperature-humidity sensor: The DHT11 is a basic, ultra low-cost digital temperature and humidity sensor. It uses a capacitive humidity sensor and a thermistor to measure the surrounding air, and spits out a digital signal on the data pin (no analog input pins needed). Its fairly simple to use, but requires careful timing to grab data. The only real downside of this sensor is you can only get new data from it once every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
